# Fritzing sketch Termometro (saved by Fritzing 0.9.3b)
breadboards: 1

parts:
  Componente1 = Arduino Uno (Rev3)
  LED1 = RGB LED (com. cathode, rgb) [package="5 mm [THT]"]
  R1 = Resistor [tolerance=±5% resistance=220 package=THT]
  R2 = Resistor [tolerance=±5% resistance=220 package=THT]
  R3 = Resistor [tolerance=±5% resistance=220 package=THT]
  IR1 = TSOP312.., 314.. [package=THT]
  J1 = Piezo Speaker
  R4 = Temperature Sensor (Thermistor) [thermistor_type=NTC package=THT]
  R5 = Resistor [tolerance=±5% resistance=220 package=THT]

nets:
  N1: Componente1.A0, R4.pin_1, R5.Pin_0
  N2: Componente1.D9_PWM, R1.Pin_1
  N3: Componente1.D10_PWM/SS, R2.Pin_1
  N4: Componente1.D11_PWM/MOSI, R3.Pin_1
  N5: Componente1.GND, LED1.common_cathode, IR1.Data, J1.pin1, R5.Pin_1
  N6: Componente1.D5_PWM, IR1.GND
  N7: Componente1.D6_PWM, J1.pin2
  N8: Componente1.5V, IR1.Vs, R4.pin_0
  N9: LED1.red_anode, R1.Pin_0
  N10: LED1.green_anode, R2.Pin_0
  N11: LED1.blue_anode, R3.Pin_0
